// Logisim project seq_circuit.circ as structural Verilog: 1 circuit, main circuit main
module main (
  input  x,
  input  y,
  output S
);

  wire and_1_out, and_2_out, C_out, clock_1_out, \D_플립플롭_q , xor_1_out;

  Clock clock_1 (.out(clock_1_out));
  xor xor_1 (xor_1_out, x, y);
  and and_1 (and_1_out, x, y);
  xor xor_2 (S, xor_1_out, \D_플립플롭_q );
  and and_2 (and_2_out, xor_1_out, \D_플립플롭_q );
  D_Flip_Flop \D_플립플롭  (.clk(clock_1_out), .D(C_out), .Q(\D_플립플롭_q ));  // open: Qn, preset, reset
  or C (C_out, and_2_out, and_1_out);
endmodule
