// Logisim project seq_circuit2.circ as structural Verilog: 1 circuit, main circuit main
module main (
  input  Q,
  input  x,
  input  y,
  output C,
  output S
);

  wire and_1_out, and_2_out, and_3_out, and_4_out, and_5_out, and_6_out, and_7_out, not_1_out, not_2_out,
       not_3_out, not_4_out, not_5_out, not_6_out;

  and and_1 (and_1_out, x, y);
  and and_2 (and_2_out, Q, y);
  and and_3 (and_3_out, Q, x);
  not not_1 (not_1_out, Q);
  not not_2 (not_2_out, x);
  not not_3 (not_3_out, Q);
  not not_4 (not_4_out, y);
  not not_5 (not_5_out, x);
  not not_6 (not_6_out, y);
  or or_1 (C, and_1_out, and_2_out, and_3_out);
  and and_4 (and_4_out, not_1_out, not_2_out, y);
  and and_5 (and_5_out, not_3_out, x, not_4_out);
  and and_6 (and_6_out, Q, not_5_out, not_6_out);
  and and_7 (and_7_out, Q, x, y);
  or or_2 (S, and_4_out, and_5_out, and_6_out, and_7_out);
endmodule
